// Digital circuit gpu.dig as structural Verilog
module gpu (
  input  clk,
  input  [15:0] in_3,
  output [15:0] out_1,
  output [7:0] out_4,
  output [15:0] out_5
);

  wire _8bit_comparator_1_eq, _8bit_counter_2_ovf, _8bit_nand_1_q, _74138_1_pin7, _74138_1_pin13,
       _74138_1_pin14, and_1_out, and_2_out, and_3_out, and_4_out, and_5_out, and_6_out, button_1_out,
       jk_ff_2_nq, load_3, load_4, load_5, nor_1_out, nor_2_out, not_1_out, not_2_out, not_3_out, not_4_out,
       not_5_out, or_1_out, or_2_out, state_char_1_done;
  wire [1:0] jk_ff_1_q;
  wire [7:0] _8bit_register_1_q, _8bit_register_2_q;
  wire [15:0] memory_ptr_1_out, sprite_ptr_1_out;

  Button button_1 (.out(button_1_out));
  or or_1 (or_1_out, jk_ff_1_q[1], jk_ff_2_nq);
  not not_1 (not_1_out, or_1_out);
  not not_2 (not_2_out, jk_ff_1_q[1]);
  and and_1 (and_1_out, _8bit_nand_1_q, jk_ff_2_nq);
  JK_FF jk_ff_1 (.J(and_2_out), .C(clk), .K(button_1_out), .Q(jk_ff_1_q[1]));  // open: nQ
  sprite_ptr sprite_ptr_1 (
    .en0(jk_ff_1_q[0]), .clk(clk), .nclr0(not_1_out), .nclr1(not_2_out), .en1(1'b1), .out(sprite_ptr_1_out));
  nor nor_1 (nor_1_out, or_2_out, _74138_1_pin7);
  memory_ptr memory_ptr_1 (
    .in0(out_4), .en(and_1_out), .nld0(load_5), .in1(out_4), .clk(clk), .nld1(load_4), .out(memory_ptr_1_out));
  Multiplexer #(.Selector_Bits(2), .Bits(16)) multiplexer_1 (
    .sel(jk_ff_1_q), .in_0(memory_ptr_1_out), .in_1(sprite_ptr_1_out), .in_2(in_3), .in_3(in_3), .out(out_5));
  JK_FF jk_ff_2 (.J(or_2_out), .C(clk), .K(nor_1_out), .Q(jk_ff_1_q[0]), .nQ(jk_ff_2_nq));
  ROM #(.AddrBits(16), .Bits(8)) rom_1 (.A(out_5), .sel(1'b1), .D(out_4));
  _74138 _74138_1 (
    .pin1(sprite_ptr_1_out[0]), .pin2(sprite_ptr_1_out[1]), .pin3(sprite_ptr_1_out[2]), .pin4(1'b0),
    .pin5(1'b0), .pin6(jk_ff_1_q[0]), .pin7(_74138_1_pin7), .pin8(1'b0), .pin10(load_5), .pin11(load_4),
    .pin12(load_3), .pin13(_74138_1_pin13), .pin14(_74138_1_pin14), .pin16(1'b1));  // open: pin9, pin15
  not not_3 (not_3_out, _74138_1_pin14);
  not not_4 (not_4_out, _74138_1_pin13);
  _8bit_register _8bit_register_1 (.clk(clk), .D(out_4), .en(not_3_out), .Q(_8bit_register_1_q));
  _8bit_register _8bit_register_2 (.clk(clk), .D(out_4), .en(not_4_out), .Q(_8bit_register_2_q));
  nor nor_2 (nor_2_out, not_4_out, _8bit_comparator_1_eq);
  _8bit_nand _8bit_nand_1 (.D(_8bit_register_1_q), .Q(_8bit_nand_1_q));
  _8bit_counter _8bit_counter_1 (
    .in(_8bit_register_1_q), .en(jk_ff_2_nq), .nld(nor_2_out), .clk(clk), .out(out_1[7:0]));  // open: ovf
  and and_2 (and_2_out, _8bit_counter_2_ovf, and_3_out);
  state_char state_char_1 (.D(out_4), .done(state_char_1_done));  // open: en, next
  or or_2 (or_2_out, _8bit_counter_2_ovf, and_4_out);
  _8bit_comparator _8bit_comparator_1 (
    .a(_8bit_register_2_q), .b(out_1[7:0]), .eq(_8bit_comparator_1_eq));  // open: gt, lt
  and and_3 (and_3_out, state_char_1_done, jk_ff_2_nq);
  and and_4 (and_4_out, _8bit_nand_1_q, and_3_out);
  _8bit_counter _8bit_counter_2 (
    .in(out_4), .en(_8bit_comparator_1_eq), .nld(load_3), .clk(clk), .out(out_1[15:8]),
    .ovf(_8bit_counter_2_ovf));
  and and_5 (and_5_out, jk_ff_2_nq, out_4[0]);
  not not_5 (not_5_out, _8bit_nand_1_q);
  and and_6 (and_6_out, not_5_out, and_3_out);
  RAMSinglePort #(.AddrBits(16), .Bits(8)) ramsingleport_1 (.A(out_1), .str(and_5_out), .C(clk), .ld(1'b0), .D(out_4));

  // Other names for the same wires on the sheet: data[7:0] = out_4

  // Notes on the sheet:
  //   clk: Hz: 30000
  //   contents of rom_1 (hex, n*v repeats v):
  //   0,ff,fe,0,0,40,0,0,0,1e,3c,30,0,50,0,0,0,a,28,3c,0,50,0,0,0,32
  //   ,50,14,0,50,0,0,0,ff,fe,0,0,41,26*0,27,4,24*0,4*49,16*0,2,6*0
  //   ,4*49,e1,f5,f5,e1,49,15*0,2,7*0,49,e1,9b,9b,e1,e1,9b,9b,49,49
  //   ,13*0,2,6*0,49,e1,e1,e1,4*9b,e1,9b,9b,49,12*0,2,5*0,49,f5,e1,e1
  //   ,4*9b,e1,e1,f5,9b,9b,49,11*0,2,4*0,49,9b,f5,f5,9b,f5,e1,f5,e1,e1
  //   ,f5,f5,f5,9b,49,11*0,2,4*0,49,e1,e1,e1,7*f5,e1,e1,9b,49,11*0,2
  //   ,5*0,49,9b,4*e1,49,e1,49,9b,9b,e1,9b,9b,49,10*0,2,4*0,9b,49,9b
  //   ,e1,e1,49,49,eb,49,eb,49,49,9b,e1,9b,49,10*0,2,4*0,49,0,49,1,49
  //   ,db,db,db,49,db,db,db,1,9b,9b,49,10*0,2,4*0,49,0,0,1,db,ff,1,eb
  //   ,db,1,ff,db,1,9b,49,11*0,2,7*0,1,db,ff,1,eb,eb,1,ff,db,1,9b,49
  //   ,11*0,2,7*0,1,db,6*eb,db,1,49,12*0,2,6*0,45,45,1,db,4*eb,db,1
  //   ,45,45,12*0,2,5*0,45,ff,ef,1,1,db,eb,eb,db,1,1,ff,ef,45,11*0,2
  //   ,5*0,45,ef,ef,9f,9f,4*1,9f,45,ef,ef,45,11*0,2,4*0,5*45,6*ef,9f
  //   ,4*45,10*0,2,4*0,45,db,db,45,9f,9f,ef,ff,ff,ff,ef,9f,45,81,db
  //   ,45,10*0,2,4*0,45,45,81,1,45,9f,9f,ef,ef,ef,9f,45,1,81,45,45,10*0
  //   ,2,4*0,45,9f,45,0,1,45,4*9f,45,1,0,45,9f,45,10*0,2,4*0,45,45,45
  //   ,1,1,9f,4*45,9f,1,1,45,45,45,10*0,2,4*0,1,eb,eb,1,45,45,9f,ff
  //   ,ef,9f,45,45,1,eb,eb,1,10*0,2,4*0,1,db,db,1,81,81,4*45,81,81,1
  //   ,db,db,1,10*0,2,5*0,1,1,1,4*81,1,81,81,81,1,1,1,11*0,2,7*0,1,81
  //   ,db,81,81,1,81,81,81,1,13*0,2,7*0,1,4*81,1,81,81,81,1,13*0,2,8*0
  //   ,1,81,81,81,1,81,81,1,14*0,2,8*0,1,81,81,81,1,81,81,1,14*0,2,8*0
  //   ,1,9f,81,81,1,81,81,1,14*0,2,8*0,1,ef,ef,9f,1,9f,9f,1,14*0,2,9*0
  //   ,7*1,14*0,2,30*0,2,30*0,2,30*0,2,30*0,2,30*0,2,30*0,2,30*0,2,30*0
  //   ,2,30*0,2,30*0,2,30*0,2,30*0,2,30*0,2,30*0,2,30*0,2,30*0,2,30*0
  //   ,2,30*0,2,30*0,2,fe
endmodule
