// Digital circuit state_char.dig as structural Verilog
module state_char (
  input  [7:0] D,
  input  en,
  output next,
  output done
);

  wire and_1_out, and_2_out, not_1_out;

  not not_1 (not_1_out, D[0]);
  and and_1 (and_1_out, not_1_out, en);
  and and_2 (and_2_out, and_1_out, D[3]);
  and and_3 (next, and_2_out, D[1]);
  and and_4 (done, and_2_out, D[2]);
endmodule
